# Fritzing sketch Sketch_BME280_ESP32-CAM (saved by Fritzing 0.8.7b)

parts:
  M2 = BME280
  Součástka1 = FTDI Basic Programmer
  Mod1 = ESP32 - CAM

nets:
  VIN: M2.VIN, Mod1.3V3
  GND: M2.GND, Součástka1.GND, Mod1.GND
  N1: M2.SCL, Mod1.IO12
  N2: M2.SDA, Mod1.IO13
  N3: Součástka1.RXI, Mod1.VOT
  N4: Součástka1.TXO, Mod1.VOR
  N5: Součástka1.POWER, Mod1.5V

notes:
  PC/Laptop
  for programming
  I2C 0x76/77
  !!! 3.3 V !!!

custom parts:
  BME280: Temperature Humidity Barometric presure Sensor
  ESP32 - CAM: The ESP32-CAM has a very competitive small-size camera module that can operate independently as a minimum system with a footprint of only 27*40.5*4.5mm and a deep sleep current of up to 6mA.
